# Fritzing sketch Devre (saved by Fritzing 0.9.5d)
breadboards: 1

parts:
  Parça1 = Arduino Nano (Rev3.0)
  OLED_I2C1 = OLED 128x64 I2C Monochrome Display
  S1 = Momentary Switch [package=ksa_sealed_tac_switch]
  S2 = Momentary Switch [package=ksa_sealed_tac_switch]
  S3 = Momentary Switch [package=ksa_sealed_tac_switch]
  S4 = Momentary Switch [package=ksa_sealed_tac_switch]
  S5 = Momentary Switch [package=ksa_sealed_tac_switch]
  S6 = Momentary Switch [package=ksa_sealed_tac_switch]
  Transceiver1 = nRF24L01 [package=module]
  S7 = Pushbutton [package="[SMD]"]

nets:
  GND: Parça1.GND, OLED_I2C1.GND, S1.4, S2.1, S2.3, S3.4, S4.1, S4.3, S5.4, S6.4, Transceiver1.GND, S7.Pin_1, S7.Pin_2
  N1: Parça1.D2, S3.2
  N2: Parça1.D3, S4.2, S4.4
  N3: Parça1.D4, S1.2
  N4: Parça1.D5, S2.2, S2.4
  N5: Parça1.D6, S6.2
  N6: Parça1.D7, S5.2
  N7: Parça1.D8, S7.Pin_3, S7.Pin_4
  N8: Parça1.D9, Transceiver1.CE
  N9: Parça1.D10, Transceiver1.CSN
  N10: Parça1.D11/MOSI, Transceiver1.MOSI
  N11: Parça1.D12/MISO, Transceiver1.MISO
  5V: Parça1.5V, OLED_I2C1.VDD, Transceiver1.VCC
  N12: Parça1.A5, OLED_I2C1.SCK
  N13: Parça1.A4, OLED_I2C1.SDA
  N14: Parça1.D13/SCK, Transceiver1.SCK

custom parts:
  nRF24L01: nRF24L01 module
